# Fritzing sketch DHT11_TempHumiditySensor_LCD_IR remote (saved by Fritzing 1.0.5)
breadboards: 1

parts:
  Elegoo_MEGA_2560 = Arduino Mega 2560 (Rev3)
  LCD_16x2 = LCD-16X2 [package=lcd-16x2]
  DHT11 = Humidity and Temperature Sensor RHT03
  TOSP_(IR_Receiver) = TSOP312.., 314.. [package=THT]
  Potentiometer = Rotary Potentiometer (Large) [maximum_resistance=10kΩ knob_status=50% power=0.5W package=THT]
  R3 = Resistor [tolerance=±5% power=0.25W resistance=220 package=THT]
  IR_LED_(Sender) = LTE-302 [package=lte-302]
  R5 = Resistor [tolerance=±5% power=0.25W resistance=220 package=THT]
  R6 = Resistor [tolerance=±5% resistance=100 package="0805 [SMD]"]
  2N2222_Transistor = NPN-Transistor [package="TO92 [THT]"]

nets (from the schematic view):
  GND: Elegoo_MEGA_2560.GND, LCD_16x2.VSS, LCD_16x2.R_W, LCD_16x2.K, DHT11.GND_2, TOSP_(IR_Receiver).GND, Potentiometer.leg2, 2N2222_Transistor.E
  N1: Elegoo_MEGA_2560.D12_PWM, LCD_16x2.RS
  N2: Elegoo_MEGA_2560.D11_PWM, LCD_16x2.E
  N3: Elegoo_MEGA_2560.D9_PWM, R6.Pin_1
  N4: Elegoo_MEGA_2560.D8_PWM, TOSP_(IR_Receiver).Data
  5V: Elegoo_MEGA_2560.5V, LCD_16x2.VDD, DHT11.Vcc, TOSP_(IR_Receiver).Vs, Potentiometer.leg1, R3.Pin_1, R5.Pin_0
  N5: Elegoo_MEGA_2560.D2_PWM, LCD_16x2.DB7
  N6: Elegoo_MEGA_2560.D3_PWM, LCD_16x2.DB6
  N7: Elegoo_MEGA_2560.D4_PWM, LCD_16x2.DB5
  N8: Elegoo_MEGA_2560.D5_PWM, LCD_16x2.DB4
  N9: Elegoo_MEGA_2560.D7_PWM, DHT11.Data-signal
  N10: LCD_16x2.VO, Potentiometer.wiper
  N11: LCD_16x2.A, R3.Pin_0
  N12: IR_LED_(Sender).A, R5.Pin_1
  N13: IR_LED_(Sender).C, 2N2222_Transistor.C
  N14: R6.Pin_0, 2N2222_Transistor.B

// code stored in the sketch: DHT11_TempHumidity_Sens-LCD_IRremote_final.ino
#include <DHT.h>
#include <LiquidCrystal.h>
#include <IRremote.hpp>

// ---- DHT11 Setup ----
#define DHTPIN 7
#define DHTTYPE DHT11
DHT dht(DHTPIN, DHTTYPE);

// ---- LCD Setup (RS, E, D4, D5, D6, D7) ----
LiquidCrystal lcd(12, 11, 5, 4, 3, 2);

// ---- IR Setup ----
const int IR_SEND_PIN = 9; // IR LED über Transistor an D9
IRsend irsend(IR_SEND_PIN);

// ---- Klima Schwellenwerte ----
const float T_ON = 22.0; // Einschalten >= 22°C
const float T_OFF = 21.0; // Ausschalten unter <= 21°C
bool klimaStatus = false; // false = aus, true = an

// Sende-Parameter ---
const uint8_t REPEATS = 12; // 8-10 ist gut
const uint16_t GAP_MS = 100; // 80-120 ms Pause zwischen Frames
const uint8_t KHZ     = 36; // erst 38Hz, bei Bedarf 36/ 40 testen

// ---- hier sind RAW-Codes - Fernbedienung ----
// AC ON
uint16_t rawOn[] = {
  3030,1620, 480,1070, 480,1120, 430,370, 480,320, 480,370, 430,1120, 430,370, 480,220, 580,1120, 430,1120, 480,370, 480,1070, 480,320, 480,370, 430,1120, 480,1070, 480,320, 480,1120, 480,1120, 480,320, 430,370, 480,1120, 430,370, 430,370, 480,320, 480,1120, 430,370, 430,370, 480,320, 480,370, 430,370, 430,370, 480,320, 480,320, 480,370, 480,320, 480,320, 480,320, 480,370, 430,370, 480,320, 480,320, 530,320, 480,320, 480,320, 480,370, 430,1120, 480,320, 480,320, 480,370, 480,320, 480,320, 480,370, 430,370, 480,1070, 480,1120, 480,320, 480,320, 480,320, 480,1120, 480,1070, 480,320, 480,370, 480,1070, 480,1120, 480,1070, 480,370, 430,370, 430,370, 430,370, 480,370, 430,320, 480,370, 430,420, 430,370, 430,370, 430,370, 480,370, 430,370, 430,370, 430,370, 430,420, 380,420, 430,370, 430,370, 480,370, 380,420, 430,370, 430,370, 430,420, 380,420, 430,370, 430,370, 480,370, 430,370, 430,370, 430,370, 430,420, 380,420, 430,370, 430,370, 480,320, 430,420, 430,370, 430,370, 430,370, 430,420, 430,370, 430,370, 430,370, 430,1170, 430,1120, 430
};

// AC OFF
uint16_t rawOff[] = {
  3030,1620, 480,1070, 480,1120, 430,370, 430,270, 530,370, 480,1120, 430,370, 480,320, 480,1120, 480,1070, 480,320, 480,1120, 430,370, 480,320, 480,1120, 430,1120, 480,320, 480,1120, 480,1070, 480,320, 530,320, 430,1120, 480,370, 430,370, 480,320, 480,1070, 480,320, 530,320, 480,320, 480,320, 480,370, 480,320, 480,320, 480,320, 480,370, 480,320, 480,320, 480,320, 480,320, 530,320, 480,320, 480,320, 480,320, 530,320, 480,370, 430,370, 430,1120, 480,370, 430,370, 430,370, 430,370, 480,370, 430,370, 430,370, 430,1170, 430,1120, 430,370, 430,370, 480,370, 430,1120, 430,1170, 380,420, 430,370, 430,1170, 380,1170, 430,1120, 480,370, 380,420, 430,370, 430,370, 480,370, 430,370, 430,370, 430,370, 430,420, 430,370, 430,370, 430,370, 480,370, 430,370, 430,370, 430,370, 480,370, 380,420, 430,370, 430,370, 480,370, 380,420, 430,370, 430,370, 480,370, 430,370, 430,370, 430,370, 430,420, 380,420, 430,370, 430,420, 430,370, 380,420, 430,370, 430,370, 480,370, 430,370, 430,370, 430,370, 430,420, 430,370, 430,370, 430,370, 480,1120, 430,1120, 430
};

// Helper: Frame mehrmals senden ---
void sendRawRepeat(uint16_t *data, size_t len, uint8_t khz, uint8_t reps) {
  for (uint8_t r = 0; r < reps; r++){
    IrSender.sendRaw(data, len, khz);
    delay(GAP_MS);
  }
}

void setup() {
  Serial.begin(115200);

  // LCD + DHT starten
  lcd.begin(16, 2);
  dht.begin();

  // IR starten
  IrSender.begin(IR_SEND_PIN, DISABLE_LED_FEEDBACK);

  lcd.print("Temp/Humidity");
  delay(2000);
  lcd.clear();
}

void loop() {
  float h = dht.readHumidity();
  float t = dht.readTemperature();

  if (isnan(h) || isnan(t)) {
    lcd.setCursor(0, 0);
    lcd.print("Sensor error ");
    delay(2000);
    return;
  }

  // Temperatur + Luftfeuchtigkeit anzeigen
  lcd.setCursor(0, 0);
  lcd.print("Temp: ");
  lcd.print(t);
  lcd.print((char)223); // Grad-Symbol
  lcd.print("C");

  lcd.setCursor(0, 1);
  lcd.print("Hum: ");
  lcd.print(h);
  lcd.print("% ");

  // ---- Klima-Logik ----
  if (!klimaStatus && t >= T_ON) {
    Serial.println("Klima EIN senden...");
    irsend.sendRaw(rawOn, sizeof(rawOn) / sizeof(rawOn[0]), 38);
    klimaStatus = true;
  }
  else if (klimaStatus && t <= T_OFF) {
    Serial.println("Klima AUS senden...");
    irsend.sendRaw(rawOff, sizeof(rawOff) / sizeof(rawOff[0]), 38);
    klimaStatus = false;
  }

  delay(3000);
}
