# Fritzing sketch VirtualFrictionSensor (saved by Fritzing 1.0.5)
breadboards: 1

parts:
  MPU-6050_(6-Ax_Gyro) = InvenSense MPU6050
  BME-280_(Temp_Humid_Pres_Sensor) = BME280 Breakout
  ESP8266_(WiFi) = Amica NodeMCU DEVKIT 1.0
  Logg_Shield_v1_0 = Memoire 1.0 - SD card log shield
  Elegoo_Mega = Arduino Mega 2560 (Rev3)
  MAX9814_(Microphone) = Breakout Board for Electret Microphone
  R1 = Resistor [tolerance=±5% resistance=1k package="0805 [SMD]"]
  R2 = Resistor [tolerance=±5% resistance=1k package="0805 [SMD]"]

nets (from the schematic view):
  VCC: MPU-6050_(6-Ax_Gyro).VCC, ESP8266_(WiFi).pin_30, Logg_Shield_v1_0.+5V, Elegoo_Mega.5V, MAX9814_(Microphone).VCC
  GND: MPU-6050_(6-Ax_Gyro).GND, MPU-6050_(6-Ax_Gyro).AD0, BME-280_(Temp_Humid_Pres_Sensor).GND, ESP8266_(WiFi).pin2, ESP8266_(WiFi).pin_25, ESP8266_(WiFi).pin_29, Logg_Shield_v1_0.N$112, Elegoo_Mega.GND, MAX9814_(Microphone).GND, R2.Pin_1
  N1: MPU-6050_(6-Ax_Gyro).SCL, Logg_Shield_v1_0.A_IN_5, Elegoo_Mega.D21/SCL, Elegoo_Mega.SCL
  N2: MPU-6050_(6-Ax_Gyro).SDA, Logg_Shield_v1_0.A_IN_4, Elegoo_Mega.D20/SDA, Elegoo_Mega.SDA
  3.3V: BME-280_(Temp_Humid_Pres_Sensor).3.3V, ESP8266_(WiFi).pin1, ESP8266_(WiFi).pin_10, ESP8266_(WiFi).pin_26, Elegoo_Mega.3V3
  N3: ESP8266_(WiFi).pin3, Elegoo_Mega.D19/RX1
  N4: ESP8266_(WiFi).pin4, R2.Pin_0
  N5: ESP8266_(WiFi).pin_27, Logg_Shield_v1_0.3V3
  N6: Logg_Shield_v1_0.DIG_10, Elegoo_Mega.D53
  N7: Logg_Shield_v1_0.DIG_11, Elegoo_Mega.D51
  N8: Logg_Shield_v1_0.DIG_12, Elegoo_Mega.D50
  N9: Logg_Shield_v1_0.DIG_13, Elegoo_Mega.D52
  N10: Elegoo_Mega.A0, MAX9814_(Microphone).AUD
  N11: Elegoo_Mega.D18/TX1, R1.Pin_0
